# Fritzing sketch TrafficLightDemo (saved by Fritzing 0.9.2b)
circuit board: 8.46667cm x 5.64444cm
breadboards: 1

parts:
  Part1 = Arduino Uno (Rev3)
  LED2 = LED - 5mm [color="Yellow (585nm)" package="5 mm [THT]"]
  LED3 = LED - 5mm [color="Green (555nm)" package="5 mm [THT]"]
  R1 = Resistor [tolerance=±5% resistance=100 package=THT]
  R2 = Resistor [tolerance=±5% resistance=100 package=THT]
  R3 = Resistor [tolerance=±5% resistance=100 package=THT]
  LED1 = LED - 5mm [color="Red (635nm)" package="5 mm [THT]"]

nets:
  N1: Part1.GND, R1.Pin_1, R2.Pin_1, R3.Pin_1
  N2: Part1.D3_PWM, LED3.anode
  N3: Part1.D4, LED2.anode
  N4: Part1.D5_PWM, LED1.anode
  N5: LED2.cathode, R2.Pin_0
  N6: LED3.cathode, R3.Pin_0
  N7: R1.Pin_0, LED1.cathode
